// Logisim project SAP1-ArchSim.circ as structural Verilog: 11 circuits, main circuit Main
module Main (
  input  RUN,
  input  [3:0] ADDRESS,
  input  [7:0] DATA
);

  wire button_1_out, button_2_out, button_3_out, clock_1_out, controlled_buffer_1_out, controller_1_cp,
       controller_1_ea, controller_1_ep, controller_1_eu, controller_1_halt, controller_1_nce,
       controller_1_nei, controller_1_nla, controller_1_nlb, controller_1_nli, controller_1_nlm,
       controller_1_nlo, controller_1_su, not_1_out, raminput_1_clk, raminput_1_ld, raminput_1_rst,
       raminput_1_str;
  wire [2:0] rom_3_data_2;
  wire [3:0] accumulator_1_h, accumulator_1_l, b_register_1_h, b_register_1_l, imar_1_toram,
       instructionregister_1_tocontroller, programcounter_1_current, raminput_1_toram, rom_2_data, rom_3_data;
  wire [6:0] rom_1_data;
  wire [6:4] rom_2_data_2;
  wire [7:0] accumulator_1_toalu, b_register_1_toalu, outputregister_1_tobindis, ram_1_data;
  wire [8:8] pull_resistor_1_node;

  ROM #(.addrWidth(9), .dataWidth(7)) rom_1 (
    .addr({pull_resistor_1_node[8], outputregister_1_tobindis}), .data(rom_1_data));  // open: sel
  Pull_Resistor pull_resistor_1 (.node(pull_resistor_1_node[8]));
  _7_Segment_Display u_7_segment_display_1 (
    .g(rom_1_data[3]), .f(rom_1_data[2]), .a(rom_1_data[1]), .b(rom_1_data[0]), .e(rom_1_data[6]),
    .d(rom_1_data[5]), .c(rom_1_data[4]));  // open: dp
  ROM #(.addrWidth(9), .dataWidth(7)) rom_2 (
    .addr({pull_resistor_1_node[8], outputregister_1_tobindis}), .data({rom_2_data_2, rom_2_data}));  // open: sel
  Button button_1 (.out(button_1_out));
  Button button_2 (.out(button_2_out));
  _7_Segment_Display u_7_segment_display_2 (
    .g(rom_2_data[3]), .f(rom_2_data[2]), .a(rom_2_data[1]), .b(rom_2_data[0]), .e(rom_2_data_2[6]),
    .d(rom_2_data_2[5]), .c(rom_2_data_2[4]));  // open: dp
  _7_Segment_Display u_7_segment_display_3 (
    .g(rom_3_data[3]), .f(rom_3_data[2]), .a(rom_3_data[1]), .b(rom_3_data[0]), .e(rom_3_data_2[2]),
    .d(rom_3_data_2[1]), .c(rom_3_data_2[0]));  // open: dp
  ROM #(.addrWidth(9), .dataWidth(7)) rom_3 (
    .addr({pull_resistor_1_node[8], outputregister_1_tobindis}), .data({rom_3_data_2, rom_3_data}));  // open: sel
  RAM #(.addrWidth(4), .bus("separate")) ram_1 (
    .addr(raminput_1_toram), .din(DATA), .data(ram_1_data), .str(raminput_1_str), .clk(raminput_1_clk),
    .ld(raminput_1_ld), .clr(raminput_1_rst));  // open: sel
  RAMInput raminput_1 (
    .Address(ADDRESS), .fromIMAR(imar_1_toram), .Run(RUN), .writeRAM(button_2_out), .CE(controller_1_nce),
    .clearRAM(button_1_out), .toRAM(raminput_1_toram), .STR(raminput_1_str), .CLK(raminput_1_clk),
    .LD(raminput_1_ld), .RST(raminput_1_rst));
  Button button_3 (.out(button_3_out));
  Hex_Digit_Display hex_digit_display_1 (.value(outputregister_1_tobindis[7:4]));  // open: dp
  Hex_Digit_Display hex_digit_display_2 (.value(outputregister_1_tobindis[3:0]));  // open: dp
  Hex_Digit_Display hex_digit_display_3 (.value(programcounter_1_current));  // open: dp
  ProgramCounter programcounter_1 (
    .Cp(controller_1_cp), .CLK(controlled_buffer_1_out), .RST(button_3_out), .Ep(controller_1_ep),
    .toBUS(ram_1_data[3:0]), .CURRENT(programcounter_1_current));
  IMAR imar_1 (
    .CLK(controlled_buffer_1_out), .CLR(button_3_out), .fromBus(ram_1_data[3:0]), .Lm(controller_1_nlm),
    .toRAM(imar_1_toram));
  InstructionRegister instructionregister_1 (
    .toController(instructionregister_1_tocontroller), .CLK(controlled_buffer_1_out), .RST(button_3_out),
    .From_Bus(ram_1_data), .Li(controller_1_nli), .toBus(ram_1_data[3:0]), .Ei(controller_1_nei));
  Controller controller_1 (
    .CLK(controlled_buffer_1_out), .I4(instructionregister_1_tocontroller[0]),
    .I5(instructionregister_1_tocontroller[1]), ._16(instructionregister_1_tocontroller[2]),
    .I7(instructionregister_1_tocontroller[3]), .Cp(controller_1_cp), .Ep(controller_1_ep),
    .nLm(controller_1_nlm), .nCE(controller_1_nce), .nLi(controller_1_nli), .nEi(controller_1_nei),
    .nLa(controller_1_nla), .Ea(controller_1_ea), .Su(controller_1_su), .Eu(controller_1_eu),
    .nLb(controller_1_nlb), .nLo(controller_1_nlo), .HALT(controller_1_halt));
  DotMatrix #(.matrixcols(8), .matrixrows(1)) dotmatrix_1 (
    .col0(ram_1_data[7]), .col1(ram_1_data[6]), .col2(ram_1_data[5]), .col3(ram_1_data[4]),
    .col4(ram_1_data[3]), .col5(ram_1_data[2]), .col6(ram_1_data[1]), .col7(ram_1_data[0]));
  Pull_Resistor pull_resistor_2 (.node(ram_1_data[7:4]));
  Clock clock_1 (.out(clock_1_out));
  not not_1 (not_1_out, controller_1_halt);
  assign controlled_buffer_1_out = not_1_out ? clock_1_out : 1'bz;  // Controlled_Buffer controlled_buffer_1
  Pull_Resistor pull_resistor_3 (.node(ram_1_data[3:0]));
  Hex_Digit_Display hex_digit_display_4 (.value(accumulator_1_h));  // open: dp
  Hex_Digit_Display hex_digit_display_5 (.value(b_register_1_h));  // open: dp
  Hex_Digit_Display hex_digit_display_6 (.value(accumulator_1_l));  // open: dp
  Hex_Digit_Display hex_digit_display_7 (.value(b_register_1_l));  // open: dp
  Accumulator accumulator_1 (
    .toALU(accumulator_1_toalu), .Ea(controller_1_ea), .CLK(controlled_buffer_1_out), .RST(button_3_out),
    .fromBus(ram_1_data), .La(controller_1_nla), .toBus(ram_1_data), .L(accumulator_1_l), .H(accumulator_1_h));
  ALU alu_1 (
    .fromBRegister(b_register_1_toalu), .toBUS(ram_1_data), .fromAccumulator(accumulator_1_toalu),
    .Su(controller_1_su), .Eu(controller_1_eu));
  B_Register b_register_1 (
    .CLK(controlled_buffer_1_out), .RST(button_3_out), .fromBus(ram_1_data), .Lb(controller_1_nlb),
    .toALU(b_register_1_toalu), .h(b_register_1_h), .l(b_register_1_l));
  OutputRegister outputregister_1 (
    .CLK(controlled_buffer_1_out), .RST(button_3_out), .fromBUS(ram_1_data), .Lo(controller_1_nlo),
    .toBINDIS(outputregister_1_tobindis));

  // Notes on the sheet:
  //   ROM AS DECODER
  //   contents of rom_1 (hex, n*v repeats v):
  //   100*0 100*11 56*6b 100*0 57*11
  //   CLR
  //   SAP-1 
  //   INSTRUCTIONS
  //   LDA 0000
  //   ADD 0001
  //   SUB 0010
  //   OUT 0011 
  //   HLT 0100
  //   contents of rom_2 (hex, n*v repeats v):
  //   10*0 10*11 10*6b 10*3b 10*1d 10*3e 10*7e 10*17 10*7f 10*3f 10*77 10*11 10*6b 10*3b 10*1d 10*3e 10*7e
  //   10*17 10*7f 10*3f 10*77 10*11 10*6b 10*3b 10*1d 6*3e 10*0 10*11 10*6b 10*3b 10*1d 10*3e 10*7e 10*17
  //   10*7f 10*3f 10*77 10*11 17*6b 10*11 10*77 10*3f 10*7f 10*17 10*7e 10*3e 10*1d 10*3b 10*6b 10*11
  //   Set RUN to HIGH to run program
  //   LOW to write program
  //   WR
  //   decimal
  //   EXAMPLE
  //   21 - 4 - 2  = 15dec : 0x0F
  //   15 + 3  + 237 = 255dec : 0xFF
  //   contents of rom_3 (hex, n*v repeats v):
  //   77 11 6b 3b 1d 3e 7e 17 7f 3f 77 11 6b 3b 1d 3e 7e 17 7f 3f 77 11 6b 3b 1d 3e 7e 17 7f 3f 77 11 6b
  //   3b 1d 3e 7e 17 7f 3f 77 11 6b 3b 1d 3e 7e 17 7f 3f 77 11 6b 3b 1d 3e 7e 17 7f 3f 77 11 6b 3b 1d 3e
  //   7e 17 7f 3f 77 11 6b 3b 1d 3e 7e 17 7f 3f 77 11 6b 3b 1d 3e 7e 17 7f 3f 77 11 6b 3b 1d 3e 7e 17 7f
  //   3f 77 11 6b 3b 1d 3e 7e 17 7f 3f 77 11 6b 3b 1d 3e 7e 17 7f 3f 77 11 6b 3b 1d 3e 7e 17 7f 3f 77 11
  //   6b 3b 1d 3e 7e 17 7f 3f 77 11 6b 3b 1d 3e 7e 17 7f 3f 77 11 6b 3b 1d 3e 7e 17 7f 3f 77 11 6b 3b 1d
  //   3e 7e 17 7f 3f 77 11 6b 3b 1d 3e 7e 17 7f 3f 77 11 6b 3b 1d 3e 7e 17 7f 3f 77 11 6b 3b 1d 3e 7e 17
  //   7f 3f 77 11 6b 3b 1d 3e 7e 17 7f 3f 77 11 6b 3b 1d 3e 7e 17 7f 3f 77 11 6b 3b 1d 3e 7e 17 7f 3f 77
  //   11 6b 3b 1d 3e 7e 17 7f 3f 77 11 6b 3b 1d 3e 7e 17 7f 3f 77 11 6b 3b 1d 3e 77 11 6b 3b 1d 3e 7e 17
  //   7f 3f 77 11 6b 3b 1d 3e 7e 17 7f 3f 77 11 6b 3b 1d 3e 7e 17 7f 3f 77 11 6b 3b 1d 3e 7e 17 7f 3f 77
  //   11 6b 3b 1d 3e 7e 17 7f 3f 77 11 6b 3b 1d 3e 7e 17 7f 3f 77 11 6b 3b 1d 3e 7e 17 7f 3f 77 11 6b 3b
  //   1d 3e 7e 17 7f 3f 77 11 6b 3b 1d 3e 7e 17 7f 3f 77 11 6b 3b 1d 3e 7e 17 7f 3f 77 11 6b 3b 1d 3e 7e
  //   17 7f 3f 77 11 6b 3b 1d 3e 7e 17 7f 3f 77 11 6b 3b 1d 3e 7e 17 7f 17 7e 3e 1d 3b 6b 11 77 3f 7f 17
  //   7e 3e 1d 3b 6b 11 77 3f 7f 17 7e 3e 1d 3b 6b 11 77 3f 7f 17 7e 3e 1d 3b 6b 11 77 3f 7f 17 7e 3e 1d
  //   3b 6b 11 77 3f 7f 17 7e 3e 1d 3b 6b 11 77 3f 7f 17 7e 3e 1d 3b 6b 11 77 3f 7f 17 7e 3e 1d 3b 6b 11
  //   77 3f 7f 17 7e 3e 1d 3b 6b 11 77 3f 7f 17 7e 3e 1d 3b 6b 11 77 3f 7f 17 7e 3e 1d 3b 6b 11 77 3f 7f
  //   17 7e 3e 1d 3b 6b 11 77 3f 7f 17 7e 3e 1d 3b 6b 11
  //   OUTPUTS
  //   hex
  //   RESET
endmodule

module ProgramCounter (
  input  Cp,
  input  CLK,
  input  RST,
  input  Ep,
  output [3:0] CURRENT,
  output [3:0] toBUS
);

  wire adder_1_out, adder_2_cout, adder_2_out, adder_3_cout, adder_3_out, adder_4_cout, adder_4_out;

  Adder #(.width(1)) adder_1 (.a(adder_2_cout), .b(CURRENT[3]), .out(adder_1_out));  // open: cin, cout
  D_Flip_Flop d_ff_1 (.clk(CLK), .D(adder_1_out), .Q(CURRENT[3]), .reset(RST));  // open: Qn, preset, en
  Adder #(.width(1)) adder_2 (.a(adder_3_cout), .b(CURRENT[2]), .out(adder_2_out), .cout(adder_2_cout));  // open: cin
  D_Flip_Flop d_ff_2 (.clk(CLK), .D(adder_2_out), .Q(CURRENT[2]), .reset(RST));  // open: Qn, preset, en
  Adder #(.width(1)) adder_3 (.a(adder_4_cout), .b(CURRENT[1]), .out(adder_3_out), .cout(adder_3_cout));  // open: cin
  Adder #(.width(1)) adder_4 (.a(Cp), .b(CURRENT[0]), .out(adder_4_out), .cout(adder_4_cout));  // open: cin
  D_Flip_Flop d_ff_3 (.clk(CLK), .D(adder_3_out), .Q(CURRENT[1]), .reset(RST));  // open: Qn, preset, en
  D_Flip_Flop d_ff_4 (.clk(CLK), .D(adder_4_out), .Q(CURRENT[0]), .reset(RST));  // open: Qn, preset, en
  LED led_1 (.in(CURRENT[2]));
  LED led_2 (.in(CURRENT[1]));
  LED led_3 (.in(CURRENT[3]));
  LED led_4 (.in(CURRENT[0]));
  assign toBUS = Ep ? CURRENT : 4'bz;  // Controlled_Buffer controlled_buffer_1

  // Notes on the sheet:
  //   PROGRAM COUNTER
endmodule

module IMAR (
  input  CLK,
  input  CLR,
  input  [3:0] fromBus,
  input  Lm,
  output [3:0] toRAM
);

  wire not_1_out;
  wire [3:0] controlled_buffer_1_out;

  assign controlled_buffer_1_out = not_1_out ? fromBus : 4'bz;  // Controlled_Buffer controlled_buffer_1
  not not_1 (not_1_out, Lm);
  D_Flip_Flop d_ff_1 (.clk(CLK), .D(controlled_buffer_1_out[3]), .Q(toRAM[3]), .reset(CLR));  // open: Qn, preset, en
  D_Flip_Flop d_ff_2 (.clk(CLK), .D(controlled_buffer_1_out[2]), .Q(toRAM[2]), .reset(CLR));  // open: Qn, preset, en
  D_Flip_Flop d_ff_3 (.clk(CLK), .D(controlled_buffer_1_out[1]), .Q(toRAM[1]), .reset(CLR));  // open: Qn, preset, en
  D_Flip_Flop D0 (.clk(CLK), .D(controlled_buffer_1_out[0]), .Q(toRAM[0]), .reset(CLR));  // open: Qn, preset, en

  // Notes on the sheet:
  //   INPUT AND MEMORY ADDRESS REGISTER
endmodule

module Controller (
  input  CLK,
  input  I4,
  input  I5,
  input  _16,
  input  I7,
  output Cp,
  output Ep,
  output nLm,
  output nCE,
  output nLi,
  output nEi,
  output nLa,
  output Ea,
  output Su,
  output Eu,
  output nLb,
  output nLo,
  output HALT
);

  wire and_1_out, and_2_out, and_3_out, and_4_out, and_5_out, and_6_out, and_7_out, and_8_out, and_9_out,
       and_10_out, and_11_out, and_12_out, and_14_out, and_16_out, and_17_out, and_18_out, d_ff_2_q,
       d_ff_3_q, d_ff_4_q, d_ff_5_q, instructiondecoder_1_add, instructiondecoder_1_lda,
       instructiondecoder_1_out, instructiondecoder_1_sub, nor_1_out;

  InstructionDecoder instructiondecoder_1 (
    .LDA(instructiondecoder_1_lda), .ADD(instructiondecoder_1_add), .SUB(instructiondecoder_1_sub),
    .OUT(instructiondecoder_1_out), .HLT(HALT), .I7(I7), .I6(_16), .I5(I5), .I4(I4));
  nor nor_1 (nor_1_out, Ep, Cp, d_ff_2_q, d_ff_3_q, d_ff_4_q, d_ff_5_q);
  and and_1 (and_1_out, d_ff_3_q, instructiondecoder_1_add);
  and and_2 (and_2_out, d_ff_3_q, instructiondecoder_1_lda);
  nor nor_2 (nLm, and_2_out, and_1_out, and_3_out, Ep);
  D_Flip_Flop D1 (.clk(CLK), .D(nor_1_out), .Q(Ep));  // open: Qn, preset, en, reset
  and and_3 (and_3_out, d_ff_3_q, instructiondecoder_1_sub);
  and and_4 (and_4_out, d_ff_4_q, instructiondecoder_1_lda);
  D_Flip_Flop d_ff_1 (.clk(CLK), .D(Ep), .Q(Cp));  // open: Qn, preset, en, reset
  and and_5 (and_5_out, instructiondecoder_1_add, d_ff_4_q);
  and and_6 (and_6_out, instructiondecoder_1_sub, d_ff_4_q);
  nor nor_3 (nCE, and_4_out, and_5_out, and_6_out, d_ff_2_q);
  D_Flip_Flop d_ff_2 (.clk(CLK), .D(Cp), .Q(d_ff_2_q));  // open: Qn, preset, en, reset
  and and_7 (and_7_out, d_ff_3_q, instructiondecoder_1_lda);
  not not_1 (nLi, d_ff_2_q);
  Hex_Digit_Display hex_digit_display_1 (.value({Cp, Ep, nLm, nCE}));  // open: dp
  Hex_Digit_Display hex_digit_display_2 (.value({nLi, nEi, nLa, Ea}));  // open: dp
  D_Flip_Flop d_ff_3 (.clk(CLK), .D(d_ff_2_q), .Q(d_ff_3_q));  // open: Qn, preset, en, reset
  and and_8 (and_8_out, d_ff_3_q, instructiondecoder_1_sub);
  and and_9 (and_9_out, d_ff_3_q, instructiondecoder_1_add);
  nor nor_4 (nEi, and_7_out, and_9_out, and_8_out);
  Hex_Digit_Display hex_digit_display_3 (.value({Su, Eu, nLb, nLo}));  // open: dp
  D_Flip_Flop d_ff_4 (.clk(CLK), .D(d_ff_3_q), .Q(d_ff_4_q));  // open: Qn, preset, en, reset
  and and_10 (and_10_out, d_ff_4_q, instructiondecoder_1_lda);
  and and_11 (and_11_out, instructiondecoder_1_add, d_ff_5_q);
  nor nor_5 (nLa, and_10_out, and_11_out, and_12_out);
  D_Flip_Flop d_ff_5 (.clk(CLK), .D(d_ff_4_q), .Q(d_ff_5_q));  // open: Qn, preset, en, reset
  and and_12 (and_12_out, instructiondecoder_1_sub, d_ff_5_q);
  and and_13 (Ea, d_ff_3_q, instructiondecoder_1_out);
  and and_14 (and_14_out, d_ff_5_q, instructiondecoder_1_add);
  and and_15 (Su, d_ff_5_q, instructiondecoder_1_sub);
  or or_1 (Eu, and_14_out, and_17_out);
  and and_16 (and_16_out, d_ff_4_q, instructiondecoder_1_add);
  and and_17 (and_17_out, d_ff_5_q, instructiondecoder_1_sub);
  nor nor_6 (nLb, and_16_out, and_18_out);
  and and_18 (and_18_out, d_ff_4_q, instructiondecoder_1_sub);
  nand nand_1 (nLo, instructiondecoder_1_out, d_ff_3_q);

  // Notes on the sheet:
  //   CONTROLLER
  //   INSTRUCTION 
  //   DECODER
  //   T0 -T6 STATES
  //   RING COUNTER
endmodule

module InstructionDecoder (
  input  I7,
  input  I6,
  input  I5,
  input  I4,
  output LDA,
  output ADD,
  output SUB,
  output OUT,
  output HLT
);

  wire not_1_out, not_2_out, not_3_out, not_4_out;

  not not_1 (not_1_out, I7);
  not not_2 (not_2_out, I6);
  not not_3 (not_3_out, I5);
  not not_4 (not_4_out, I4);
  and and_1 (LDA, not_4_out, not_3_out, not_2_out, not_1_out);
  and and_2 (ADD, I4, not_3_out, not_2_out, not_1_out);
  and and_3 (SUB, not_4_out, I5, not_2_out, not_1_out);
  and and_4 (OUT, I4, I5, not_2_out, not_1_out);
  and and_5 (HLT, not_4_out, not_3_out, I6, not_1_out);

  // Notes on the sheet:
  //   LDA 0000
  //   ADD 0001
  //   SUB 0010
  //   OUT 0011 
  //   HLT 0100
endmodule

module InstructionRegister (
  input  Ei,
  input  CLK,
  input  RST,
  input  [7:0] From_Bus,
  input  Li,
  output [3:0] toBus,
  output [3:0] toController
);

  wire not_1_out, not_2_out;
  wire [3:0] D0_q;
  wire [7:0] controlled_buffer_1_out;

  D_Flip_Flop D7 (.clk(CLK), .D(controlled_buffer_1_out[7]), .Q(toController[3]), .reset(RST));  // open: Qn, preset, en
  D_Flip_Flop d_ff_1 (
    .clk(CLK), .D(controlled_buffer_1_out[6]), .Q(toController[2]), .reset(RST));  // open: Qn, preset, en
  assign controlled_buffer_1_out = not_1_out ? From_Bus : 8'bz;  // Controlled_Buffer controlled_buffer_1
  not not_1 (not_1_out, Li);
  D_Flip_Flop d_ff_2 (
    .clk(CLK), .D(controlled_buffer_1_out[5]), .Q(toController[1]), .reset(RST));  // open: Qn, preset, en
  D_Flip_Flop d_ff_3 (
    .clk(CLK), .D(controlled_buffer_1_out[4]), .Q(toController[0]), .reset(RST));  // open: Qn, preset, en
  D_Flip_Flop d_ff_4 (.clk(CLK), .D(controlled_buffer_1_out[3]), .Q(D0_q[3]), .reset(RST));  // open: Qn, preset, en
  D_Flip_Flop d_ff_5 (.clk(CLK), .D(controlled_buffer_1_out[2]), .Q(D0_q[2]), .reset(RST));  // open: Qn, preset, en
  assign toBus = not_2_out ? D0_q : 4'bz;  // Controlled_Buffer controlled_buffer_2
  not not_2 (not_2_out, Ei);
  D_Flip_Flop d_ff_6 (.clk(CLK), .D(controlled_buffer_1_out[1]), .Q(D0_q[1]), .reset(RST));  // open: Qn, preset, en
  D_Flip_Flop D0 (.clk(CLK), .D(controlled_buffer_1_out[0]), .Q(D0_q[0]), .reset(RST));  // open: Qn, preset, en
endmodule

module OutputRegister (
  input  CLK,
  input  RST,
  input  [7:0] fromBUS,
  input  Lo,
  output [7:0] toBINDIS
);

  wire not_1_out;
  wire [7:0] controlled_buffer_1_out;

  D_Flip_Flop D7 (.clk(CLK), .D(controlled_buffer_1_out[7]), .Q(toBINDIS[7]), .reset(RST));  // open: Qn, preset, en
  assign controlled_buffer_1_out = not_1_out ? fromBUS : 8'bz;  // Controlled_Buffer controlled_buffer_1
  not not_1 (not_1_out, Lo);
  D_Flip_Flop d_ff_1 (.clk(CLK), .D(controlled_buffer_1_out[6]), .Q(toBINDIS[6]), .reset(RST));  // open: Qn, preset, en
  D_Flip_Flop d_ff_2 (.clk(CLK), .D(controlled_buffer_1_out[5]), .Q(toBINDIS[5]), .reset(RST));  // open: Qn, preset, en
  D_Flip_Flop d_ff_3 (.clk(CLK), .D(controlled_buffer_1_out[4]), .Q(toBINDIS[4]), .reset(RST));  // open: Qn, preset, en
  D_Flip_Flop d_ff_4 (.clk(CLK), .D(controlled_buffer_1_out[3]), .Q(toBINDIS[3]), .reset(RST));  // open: Qn, preset, en
  D_Flip_Flop d_ff_5 (.clk(CLK), .D(controlled_buffer_1_out[2]), .Q(toBINDIS[2]), .reset(RST));  // open: Qn, preset, en
  D_Flip_Flop d_ff_6 (.clk(CLK), .D(controlled_buffer_1_out[1]), .Q(toBINDIS[1]), .reset(RST));  // open: Qn, preset, en
  D_Flip_Flop D0 (.clk(CLK), .D(controlled_buffer_1_out[0]), .Q(toBINDIS[0]), .reset(RST));  // open: Qn, preset, en
endmodule

module Accumulator (
  input  Ea,
  input  CLK,
  input  RST,
  input  [7:0] fromBus,
  input  La,
  output [3:0] H,
  output [3:0] L,
  output [7:0] toALU,
  output [7:0] toBus
);

  wire not_1_out;
  wire [7:0] controlled_buffer_1_out;

  D_Flip_Flop D7 (.clk(CLK), .D(controlled_buffer_1_out[7]), .Q(H[3]), .reset(RST));  // open: Qn, preset, en
  assign controlled_buffer_1_out = not_1_out ? fromBus : 8'bz;  // Controlled_Buffer controlled_buffer_1
  not not_1 (not_1_out, La);
  D_Flip_Flop d_ff_1 (.clk(CLK), .D(controlled_buffer_1_out[6]), .Q(H[2]), .reset(RST));  // open: Qn, preset, en
  D_Flip_Flop d_ff_2 (.clk(CLK), .D(controlled_buffer_1_out[5]), .Q(H[1]), .reset(RST));  // open: Qn, preset, en
  assign toBus = Ea ? {H, L} : 8'bz;  // Controlled_Buffer controlled_buffer_2
  D_Flip_Flop d_ff_3 (.clk(CLK), .D(controlled_buffer_1_out[4]), .Q(H[0]), .reset(RST));  // open: Qn, preset, en
  D_Flip_Flop d_ff_4 (.clk(CLK), .D(controlled_buffer_1_out[3]), .Q(L[3]), .reset(RST));  // open: Qn, preset, en
  D_Flip_Flop d_ff_5 (.clk(CLK), .D(controlled_buffer_1_out[2]), .Q(L[2]), .reset(RST));  // open: Qn, preset, en
  D_Flip_Flop d_ff_6 (.clk(CLK), .D(controlled_buffer_1_out[1]), .Q(L[1]), .reset(RST));  // open: Qn, preset, en
  D_Flip_Flop D0 (.clk(CLK), .D(controlled_buffer_1_out[0]), .Q(L[0]), .reset(RST));  // open: Qn, preset, en

  assign toALU = {H, L};
endmodule

module B_Register (
  input  CLK,
  input  RST,
  input  [7:0] fromBus,
  input  Lb,
  output [3:0] h,
  output [3:0] l,
  output [7:0] toALU
);

  wire not_1_out;
  wire [7:0] controlled_buffer_1_out;

  D_Flip_Flop D7 (.clk(CLK), .D(controlled_buffer_1_out[7]), .Q(h[3]), .reset(RST));  // open: Qn, preset, en
  assign controlled_buffer_1_out = not_1_out ? fromBus : 8'bz;  // Controlled_Buffer controlled_buffer_1
  not not_1 (not_1_out, Lb);
  D_Flip_Flop d_ff_1 (.clk(CLK), .D(controlled_buffer_1_out[6]), .Q(h[2]), .reset(RST));  // open: Qn, preset, en
  D_Flip_Flop d_ff_2 (.clk(CLK), .D(controlled_buffer_1_out[5]), .Q(h[1]), .reset(RST));  // open: Qn, preset, en
  D_Flip_Flop d_ff_3 (.clk(CLK), .D(controlled_buffer_1_out[4]), .Q(h[0]), .reset(RST));  // open: Qn, preset, en
  D_Flip_Flop d_ff_4 (.clk(CLK), .D(controlled_buffer_1_out[3]), .Q(l[3]), .reset(RST));  // open: Qn, preset, en
  D_Flip_Flop d_ff_5 (.clk(CLK), .D(controlled_buffer_1_out[2]), .Q(l[2]), .reset(RST));  // open: Qn, preset, en
  D_Flip_Flop d_ff_6 (.clk(CLK), .D(controlled_buffer_1_out[1]), .Q(l[1]), .reset(RST));  // open: Qn, preset, en
  D_Flip_Flop D0 (.clk(CLK), .D(controlled_buffer_1_out[0]), .Q(l[0]), .reset(RST));  // open: Qn, preset, en

  assign toALU = {h, l};
endmodule

module ALU (
  input  [7:0] fromBRegister,
  input  Su,
  input  Eu,
  input  [7:0] fromAccumulator,
  output [7:0] toBUS
);

  wire adder_1_cout, adder_3_cout, adder_4_cout, adder_5_cout, adder_6_cout, adder_7_cout, adder_8_cout,
       xor_1_out, xor_2_out, xor_3_out, xor_4_out, xor_5_out, xor_6_out, xor_7_out, xor_8_out;
  wire [7:0] adder_8_out;

  assign toBUS = Eu ? adder_8_out : 8'bz;  // Controlled_Buffer controlled_buffer_1
  xor xor_1 (xor_1_out, Su, fromBRegister[7]);
  xor xor_2 (xor_2_out, Su, fromBRegister[6]);
  Adder #(.width(1)) adder_1 (
    .a(xor_2_out), .b(fromAccumulator[6]), .out(adder_8_out[6]), .cin(adder_3_cout), .cout(adder_1_cout));
  Adder #(.width(1)) adder_2 (
    .a(xor_1_out), .b(fromAccumulator[7]), .out(adder_8_out[7]), .cin(adder_1_cout));  // open: cout
  xor xor_3 (xor_3_out, Su, fromBRegister[5]);
  Adder #(.width(1)) adder_3 (
    .a(xor_3_out), .b(fromAccumulator[5]), .out(adder_8_out[5]), .cin(adder_4_cout), .cout(adder_3_cout));
  xor xor_4 (xor_4_out, Su, fromBRegister[3]);
  xor xor_5 (xor_5_out, Su, fromBRegister[4]);
  Adder #(.width(1)) adder_4 (
    .a(xor_5_out), .b(fromAccumulator[4]), .out(adder_8_out[4]), .cin(adder_5_cout), .cout(adder_4_cout));
  xor xor_6 (xor_6_out, Su, fromBRegister[2]);
  Adder #(.width(1)) adder_5 (
    .a(xor_4_out), .b(fromAccumulator[3]), .out(adder_8_out[3]), .cin(adder_6_cout), .cout(adder_5_cout));
  xor xor_7 (xor_7_out, Su, fromBRegister[1]);
  Adder #(.width(1)) adder_6 (
    .a(xor_6_out), .b(fromAccumulator[2]), .out(adder_8_out[2]), .cin(adder_7_cout), .cout(adder_6_cout));
  xor xor_8 (xor_8_out, Su, fromBRegister[0]);
  Adder #(.width(1)) adder_7 (
    .a(xor_7_out), .b(fromAccumulator[1]), .out(adder_8_out[1]), .cin(adder_8_cout), .cout(adder_7_cout));
  Adder #(.width(1)) adder_8 (
    .a(xor_8_out), .b(fromAccumulator[0]), .out(adder_8_out[0]), .cin(Su), .cout(adder_8_cout));
endmodule

module RAMInput (
  input  [3:0] Address,
  input  [3:0] fromIMAR,
  input  Run,
  input  writeRAM,
  input  CE,
  input  clearRAM,
  output [3:0] toRAM,
  output STR,
  output CLK,
  output LD,
  output RST
);

  Multiplexer #(.width(4)) multiplexer_1 (.in0(Address), .in1(fromIMAR), .out(toRAM), .sel(Run));  // open: en
  not not_1 (STR, Run);
  not not_2 (LD, CE);
  and and_1 (CLK, ~Run, writeRAM);  // AND_Gate
  and and_2 (RST, ~Run, clearRAM);  // AND_Gate
endmodule
